// Logisim project ALU.circ as structural Verilog: 2 circuits, main circuit main
module main (
);

  ALU alu_1 ();  // open: A, B, R
endmodule

module ALU (
  input  [7:0] A,
  input  [7:0] B,
  output [7:0] R
);

  wire clock_1_out, undriven;
  wire [7:0] adder_1_out, and_1_out, IR_HI_q, MAR_q, multiplexer_1_out, nand_1_out, or_1_out, PC_q,
       subtractor_1_out, xor_1_out;
  wire [15:0] IR_q, MDR_q, ram_1_dout;

  Register PC (.Q(PC_q));  // open: D, en, clk, clr
  Register MAR (.D(PC_q), .Q(MAR_q));  // open: en, clk, clr
  RAM #(.dataWidth(16)) ram_1 (.addr(MAR_q), .we(1'b1), .oe(1'b1), .clk(clock_1_out), .dout(ram_1_dout));  // open: din
  Clock clock_1 (.out(clock_1_out));
  Register #(.width(16)) MDR (.D(ram_1_dout), .Q(MDR_q));  // open: en, clk, clr
  Register #(.width(16)) IR (.D(MDR_q), .Q(IR_q));  // open: en, clk, clr
  Subtractor subtractor_1 (.a(A), .b(B), .out(subtractor_1_out));  // open: bin, bout
  Adder adder_1 (.a(A), .b(B), .out(adder_1_out));  // open: cin, cout
  assign and_1_out = A & B;  // AND_Gate and_1, 8 bits wide
  assign or_1_out = A | B;  // OR_Gate or_1, 8 bits wide
  assign nand_1_out = ~(A & B);  // NAND_Gate nand_1, 8 bits wide
  assign xor_1_out = A ^ B;  // XOR_Gate xor_1, 8 bits wide
  Register IR_LOW (.D(IR_q[7:0]), .Q(B));  // open: en, clk, clr
  Register IR_HI (.D(IR_q[15:8]), .Q(IR_HI_q));  // open: en, clk, clr
  Multiplexer #(.select(4), .width(8)) multiplexer_1 (
    .in4(subtractor_1_out), .in5(adder_1_out), .in6(and_1_out), .in7(or_1_out), .in8(nand_1_out),
    .in9(xor_1_out), .out(multiplexer_1_out), .sel(IR_HI_q[7:4]));  // open: in0, in1, in2, in3, in10, in11, in12, in13, in14, in15
  Register Acum (.D(multiplexer_1_out), .Q(R), .clr(undriven));  // open: en, clk
endmodule
