// Logisim project ALU_2.circ as structural Verilog: 1 circuit, main circuit main
module main (
  input  [7:0] A,
  input  [7:0] B,
  output [7:0] R
);

  wire clock_1_out, multiplexer_1_p9, undriven;
  wire [7:0] adder_1_out, and_1_out, IR_HI_q, multiplexer_1_p11, nand_1_out, or_1_out, PC_q, rom_1_data,
       subtractor_1_out, xor_1_out;
  wire [15:0] IR_q, MDR_q, ram_1_dout;

  Register PC (.en(rom_1_data[6]), .Q(PC_q));  // open: D, clk, clr
  Register MAR (.en(rom_1_data[1]), .Q(PC_q));  // open: D, clk, clr
  RAM #(.dataWidth(16)) ram_1 (
    .addr(PC_q), .we(rom_1_data[7]), .oe(rom_1_data[2]), .clk(clock_1_out), .dout(ram_1_dout));  // open: din
  Clock clock_1 (.out(clock_1_out));
  Register #(.width(16)) MDR (.D(ram_1_dout), .en(rom_1_data[3]), .Q(MDR_q));  // open: clk, clr
  Register #(.width(16)) IR (.D(MDR_q), .Q(IR_q));  // open: en, clk, clr
  Subtractor subtractor_1 (.a(A), .b(B), .out(subtractor_1_out));  // open: bin, bout
  Adder adder_1 (.a(A), .b(B), .out(adder_1_out));  // open: cin, cout
  assign and_1_out = A & B;  // AND_Gate and_1, 8 bits wide
  assign or_1_out = A | B;  // OR_Gate or_1, 8 bits wide
  assign nand_1_out = ~(A & B);  // NAND_Gate nand_1, 8 bits wide
  assign xor_1_out = A ^ B;  // XOR_Gate xor_1, 8 bits wide
  Register IR_LOW (.D(IR_q[7:0]), .Q(B));  // open: en, clk, clr
  Register IR_HI (.D(IR_q[15:8]), .Q(IR_HI_q));  // open: en, clk, clr
  // Multiplexer #(.select(4), .width(8)) multiplexer_1: pin names not known; wires that end beside it: subtractor_1_out, adder_1_out, and_1_out, or_1_out, nand_1_out, xor_1_out, rom_1_data[4], rom_1_data[5], multiplexer_1_p9, multiplexer_1_p9, multiplexer_1_p11
  ROM rom_1 (.addr(IR_HI_q), .data(rom_1_data));
  Register Acum (.D(multiplexer_1_p11), .en(rom_1_data[0]), .Q(R), .clr(undriven));  // open: clk
endmodule
